// Logisim project 8 bits Write gate-sym.circ as structural Verilog: 1 circuit, main circuit main
module main (
  input  [7:0] Data_In,
  input  Write,
  output [7:0] Data_Out
);

  Register #(.trigger("high")) register_1 (.D(Data_In), .Q(Data_Out), .clk(Write));  // open: en, clr

  // Notes on the sheet:
  //   DI0
  //   DI7
  //   DO7
  //   DO0
endmodule
