// Logisim project 8 bits Write gate.circ as structural Verilog: 1 circuit, main circuit main
module main (
  input  Write,
  input  DI0,
  input  DI1,
  input  DI2,
  input  DI3,
  input  DI4,
  input  DI5,
  input  DI6,
  input  DI7,
  output DO0,
  output DO1,
  output DO2,
  output DO3,
  output DO4,
  output DO5,
  output DO6,
  output DO7
);

  D_Flip_Flop #(.trigger("high")) d_ff_1 (.clk(Write), .D(DI0), .Q(DO0));  // open: Qn, preset, en, reset
  D_Flip_Flop #(.trigger("high")) d_ff_2 (.clk(Write), .D(DI1), .Q(DO1));  // open: Qn, preset, en, reset
  D_Flip_Flop #(.trigger("high")) d_ff_3 (.clk(Write), .D(DI2), .Q(DO2));  // open: Qn, preset, en, reset
  D_Flip_Flop #(.trigger("high")) d_ff_4 (.clk(Write), .D(DI3), .Q(DO3));  // open: Qn, preset, en, reset
  D_Flip_Flop #(.trigger("high")) d_ff_5 (.clk(Write), .D(DI4), .Q(DO4));  // open: Qn, preset, en, reset
  D_Flip_Flop #(.trigger("high")) d_ff_6 (.clk(Write), .D(DI5), .Q(DO5));  // open: Qn, preset, en, reset
  D_Flip_Flop #(.trigger("high")) d_ff_7 (.clk(Write), .D(DI6), .Q(DO6));  // open: Qn, preset, en, reset
  D_Flip_Flop #(.trigger("high")) d_ff_8 (.clk(Write), .D(DI7), .Q(DO7));  // open: Qn, preset, en, reset
endmodule
