// Logisim project Circuit.circ as structural Verilog: 1 circuit, main circuit main
module main (
  input  Haut,
  input  Bas,
  input  Start,
  output Recule,
  output Avance
);

  wire and_1_out, and_2_out, and_3_out, and_4_out, clock_1_out, d_ff_1_qn, d_ff_2_qn, not_1_out, not_2_out,
       or_1_out, or_2_out;

  not not_1 (not_1_out, Haut);
  not not_2 (not_2_out, Bas);
  and and_1 (and_1_out, Avance, d_ff_1_qn, Bas);
  and and_2 (and_2_out, not_1_out, Recule, d_ff_2_qn);
  and and_3 (and_3_out, d_ff_1_qn, Start, d_ff_2_qn);
  and and_4 (and_4_out, not_2_out, d_ff_1_qn, Avance);
  or or_1 (or_1_out, and_1_out, and_2_out);
  or or_2 (or_2_out, and_3_out, and_4_out);
  Clock clock_1 (.out(clock_1_out));
  D_Flip_Flop d_ff_1 (.clk(clock_1_out), .D(or_1_out), .Q(Recule), .Qn(d_ff_1_qn));  // open: preset, en, reset
  D_Flip_Flop d_ff_2 (.clk(clock_1_out), .D(or_2_out), .Q(Avance), .Qn(d_ff_2_qn));  // open: preset, en, reset
endmodule
