// Logisim project Compteur-Registre.circ as structural Verilog: 1 circuit, main circuit main
module main (
  output [7:0] out_1,
  output [7:0] out_2
);

  wire clock_1_out;

  Clock clock_1 (.out(clock_1_out));
  Register register_1 (.D(out_2), .Q(out_1), .clk(clock_1_out));  // open: en, clr
  Adder adder_1 (.a(out_1), .b(8'h1), .out(out_2));  // open: cin, cout
endmodule
