// Logisim project D Flip Flop.circ as structural Verilog: 1 circuit, main circuit main
module main (
  input  in_1,
  output out_2,
  output out_3
);

  wire clock_1_out, not_1_out;

  Clock clock_1 (.out(clock_1_out));
  D_Flip_Flop #(.trigger("high")) d_ff_1 (.clk(not_1_out), .D(in_1), .Q(out_3));  // open: Qn, preset, en, reset
  not not_1 (not_1_out, clock_1_out);
  D_Flip_Flop #(.trigger("high")) d_ff_2 (.clk(clock_1_out), .D(out_3), .Q(out_2));  // open: Qn, preset, en, reset
endmodule
