// Logisim project D Latch-sym.circ as structural Verilog: 1 circuit, main circuit main
module main (
  input  G,
  input  D,
  output Q
);

  D_Flip_Flop #(.trigger("high")) d_ff_1 (.clk(G), .D(D), .Q(Q));  // open: Qn, preset, en, reset
endmodule
