// Logisim project D Latch.circ as structural Verilog: 1 circuit, main circuit main
module main (
  input  D,
  input  G,
  output Q
);

  Multiplexer #(.disabled(0), .enable("false")) multiplexer_1 (.in0(Q), .in1(D), .out(Q), .sel(G));

  // Notes on the sheet:
  //   Q'
endmodule
