// Logisim project Décodeur.circ as structural Verilog: 1 circuit, main circuit main
module main (
  input  Data_In,
  input  [2:0] Address,
  output DO0,
  output DO1,
  output DO2,
  output DO3,
  output DO4,
  output DO5,
  output DO6,
  output DO7
);

  Demultiplexer #(.select(3), .enable("false")) demultiplexer_1 (
    .out0(DO0), .out1(DO1), .out2(DO2), .out3(DO3), .out4(DO4), .out5(DO5), .out6(DO6), .out7(DO7),
    .in(Data_In), .sel(Address));
endmodule
