// Logisim project Fibonacci.circ as structural Verilog: 1 circuit, main circuit main
module main (
  output [7:0] out_1,
  output [7:0] out_2,
  output [7:0] C,
  output [7:0] out_4
);

  wire clock_1_out, not_1_out, not_2_out;

  Clock clock_1 (.out(clock_1_out));
  not not_1 (not_1_out, clock_1_out);
  Register register_1 (.D(C), .Q(out_1), .clk(not_1_out));  // open: en, clr
  Register register_2 (.D(out_1), .Q(out_4), .clk(not_1_out));  // open: en, clr
  Adder adder_1 (.a(out_1), .b(out_4), .out(out_2));  // open: cin, cout
  not not_2 (not_2_out, not_1_out);
  Register register_3 (.D(out_2), .Q(C), .clk(not_2_out));  // open: en, clr

  // Notes on the sheet:
  //   B
  //   A
  //   Remarque : pour intitialiser l'exécution, il faut charger 1 dans le registre B
endmodule
