// Logisim project RAM 16x1 bits - sym.circ as structural Verilog: 1 circuit, main circuit main
module main (
  input  Data_In,
  input  Write,
  input  [3:0] Address,
  output Data_Out
);

  wire not_1_out;

  assign Data_Out = Write ? Data_In : 1'bz;  // Controlled_Buffer controlled_buffer_1
  not not_1 (not_1_out, Write);
  RAM #(.addrWidth(4), .dataWidth(1), .bus("asynch")) ram_1 (
    .addr(Address), .data(Data_Out), .ld(not_1_out));  // open: sel, clr
endmodule
