// Logisim project RAM 16x1 bits.circ as structural Verilog: 1 circuit, main circuit main
module main (
  input  Data_In,
  input  Select_Byte,
  input  Write,
  input  [2:0] Address,
  output Data_Out
);

  wire controlled_buffer_1_out, controlled_buffer_2_out, demultiplexer_1_out0, demultiplexer_1_out1,
       not_1_out, not_2_out;

  Demultiplexer #(.enable("false")) demultiplexer_1 (
    .out0(demultiplexer_1_out0), .out1(demultiplexer_1_out1), .in(Data_In), .sel(Select_Byte));
  assign controlled_buffer_1_out = Write ? demultiplexer_1_out0 : 1'bz;  // Controlled_Buffer controlled_buffer_1
  assign controlled_buffer_2_out = Write ? demultiplexer_1_out1 : 1'bz;  // Controlled_Buffer controlled_buffer_2
  not not_1 (not_1_out, Write);
  not not_2 (not_2_out, Write);
  RAM #(.addrWidth(3), .dataWidth(1), .bus("asynch")) ram_1 (
    .addr(Address), .data(controlled_buffer_1_out), .ld(not_1_out));  // open: sel, clr
  RAM #(.addrWidth(3), .dataWidth(1), .bus("asynch")) ram_2 (
    .addr(Address), .data(controlled_buffer_2_out), .ld(not_2_out));  // open: sel, clr
  Multiplexer #(.enable("false")) multiplexer_1 (
    .in0(controlled_buffer_1_out), .in1(controlled_buffer_2_out), .out(Data_Out), .sel(Select_Byte));
endmodule
