// Logisim project RAM 8x2 bits - sym.circ as structural Verilog: 1 circuit, main circuit main
module main (
  input  [1:0] Data_In,
  input  Write,
  input  [2:0] Address,
  output [1:0] Data_Out
);

  wire not_1_out;

  assign Data_Out = Write ? Data_In : 2'bz;  // Controlled_Buffer controlled_buffer_1
  not not_1 (not_1_out, Write);
  RAM #(.addrWidth(3), .dataWidth(2), .bus("asynch")) ram_1 (
    .addr(Address), .data(Data_Out), .ld(not_1_out));  // open: sel, clr
endmodule
