// Logisim project RAM 8x2 bits.circ as structural Verilog: 1 circuit, main circuit main
module main (
  input  DI0,
  input  DI1,
  input  Write,
  input  [2:0] Address,
  output DO0,
  output DO1
);

  wire not_1_out, not_2_out;

  assign DO0 = Write ? DI0 : 1'bz;  // Controlled_Buffer controlled_buffer_1
  assign DO1 = Write ? DI1 : 1'bz;  // Controlled_Buffer controlled_buffer_2
  not not_1 (not_1_out, Write);
  not not_2 (not_2_out, Write);
  RAM #(.addrWidth(3), .dataWidth(1), .bus("asynch")) ram_1 (
    .addr(Address), .data(DO0), .ld(not_1_out));  // open: sel, clr
  RAM #(.addrWidth(3), .dataWidth(1), .bus("asynch")) ram_2 (
    .addr(Address), .data(DO1), .ld(not_2_out));  // open: sel, clr
endmodule
