// Logisim project SommeRAM.circ as structural Verilog: 1 circuit, main circuit main
module main (
  output [7:0] out_1
);

  wire button_1_out, Horloge_out;
  wire [3:0] Compteur_q;
  wire [7:0] adder_1_out, register_1_q;

  Clock Horloge (.out(Horloge_out));
  Button button_1 (.out(button_1_out));
  Counter #(.width(4), .max('hf)) Compteur (
    .Q(Compteur_q), .clk(Horloge_out), .clr(button_1_out));  // open: load, D, count, carry
  RAM #(.addrWidth(4)) ram_1 (.addr(Compteur_q), .data(out_1), .clk(Horloge_out));  // open: sel, ld, clr
  Adder adder_1 (.a(out_1), .b(register_1_q), .out(adder_1_out));  // open: cin, cout
  Register register_1 (.D(adder_1_out), .Q(register_1_q), .clk(Horloge_out), .clr(button_1_out));  // open: en
  // Probe on register_1_q

  // Notes on the sheet:
  //   Reset
  //   RAM 16 x 8 bits
  //   Additionneur 8 bits
  //   Accumulateur
endmodule
