// Logisim project Sélecteur.circ as structural Verilog: 1 circuit, main circuit main
module main (
  input  DI0,
  input  DI1,
  input  DI2,
  input  DI3,
  input  DI4,
  input  DI5,
  input  DI6,
  input  DI7,
  input  [2:0] Address,
  output Data_Out
);

  Multiplexer #(.select(3), .enable("false")) multiplexer_1 (
    .in0(DI0), .in1(DI1), .in2(DI2), .in3(DI3), .in4(DI4), .in5(DI5), .in6(DI6), .in7(DI7), .out(Data_Out),
    .sel(Address));
endmodule
