// Logisim project Verrou-sequentiel.circ as structural Verilog: 1 circuit, main circuit main
module main (
  input  D,
  input  G,
  output Q
);

  wire and_1_out, and_2_out, clock_1_out, not_1_out, or_1_out;

  not not_1 (not_1_out, G);
  and and_1 (and_1_out, D, G);
  and and_2 (and_2_out, not_1_out, Q);
  Clock clock_1 (.out(clock_1_out));
  or or_1 (or_1_out, and_1_out, and_2_out);
  D_Flip_Flop d_ff_1 (.clk(clock_1_out), .D(or_1_out), .Q(Q));  // open: Qn, preset, en, reset
endmodule
