// Logisim project Write gate.circ as structural Verilog: 1 circuit, main circuit main
module main (
  input  Write,
  input  Data_In,
  output Data_Out
);

  D_Flip_Flop d_ff_1 (.clk(Write), .D(Data_In), .Q(Data_Out));  // open: Qn, preset, en, reset
endmodule
