// Logisim project add1bit-sym.circ as structural Verilog: 1 circuit, main circuit main
module main (
  input  c_in,
  input  a,
  input  b,
  output s,
  output c_out
);

  Adder #(.width(1)) adder_1 (.a(a), .b(b), .out(s), .cin(c_in), .cout(c_out));
endmodule
