// Logisim project add1bit.circ as structural Verilog: 1 circuit, main circuit main
module main (
  input  a,
  input  b,
  input  c_in,
  output c_out,
  output s
);

  wire and_1_out, and_2_out, and_3_out, and_4_out, and_5_out, and_6_out, and_7_out, not_1_out, not_2_out,
       not_3_out, not_4_out, not_5_out, not_6_out;

  not not_1 (not_1_out, b);
  not not_2 (not_2_out, c_in);
  not not_3 (not_3_out, a);
  not not_4 (not_4_out, c_in);
  not not_5 (not_5_out, a);
  not not_6 (not_6_out, b);
  and and_1 (and_1_out, a, b);
  and and_2 (and_2_out, b, c_in);
  and and_3 (and_3_out, a, c_in);
  and and_4 (and_4_out, a, not_1_out, not_2_out);
  and and_5 (and_5_out, not_3_out, b, not_4_out);
  and and_6 (and_6_out, not_5_out, not_6_out, c_in);
  and and_7 (and_7_out, a, b, c_in);
  or or_1 (c_out, and_1_out, and_2_out, and_3_out);
  or or_2 (s, and_4_out, and_5_out, and_6_out, and_7_out);
endmodule
