// Logisim project add8bit.circ as structural Verilog: 1 circuit, main circuit main
module main (
  input  a7,
  input  a6,
  input  a5,
  input  a4,
  input  a3,
  input  a2,
  input  a1,
  input  a0,
  input  b7,
  input  b6,
  input  b5,
  input  b4,
  input  b3,
  input  b2,
  input  b1,
  input  b0,
  output retenue,
  output s7,
  output s6,
  output s5,
  output s4,
  output s3,
  output s2,
  output s1,
  output s0
);

  wire adder_2_cout, adder_3_cout, adder_4_cout, adder_5_cout, adder_6_cout, adder_7_cout, adder_8_cout;

  Adder #(.width(1)) adder_1 (.a(a7), .b(b7), .out(s7), .cin(adder_2_cout), .cout(retenue));
  Adder #(.width(1)) adder_2 (.a(a6), .b(b6), .out(s6), .cin(adder_3_cout), .cout(adder_2_cout));
  Adder #(.width(1)) adder_3 (.a(a5), .b(b5), .out(s5), .cin(adder_4_cout), .cout(adder_3_cout));
  Adder #(.width(1)) adder_4 (.a(a4), .b(b4), .out(s4), .cin(adder_5_cout), .cout(adder_4_cout));
  Adder #(.width(1)) adder_5 (.a(a3), .b(b3), .out(s3), .cin(adder_6_cout), .cout(adder_5_cout));
  Adder #(.width(1)) adder_6 (.a(a2), .b(b2), .out(s2), .cin(adder_7_cout), .cout(adder_6_cout));
  Adder #(.width(1)) adder_7 (.a(a1), .b(b1), .out(s1), .cin(adder_8_cout), .cout(adder_7_cout));
  Adder #(.width(1)) adder_8 (.a(a0), .b(b0), .out(s0), .cin(1'b0), .cout(adder_8_cout));
endmodule
