// Logisim project retenue.circ as structural Verilog: 1 circuit, main circuit main
module main (
  input  a,
  input  b,
  input  c_in,
  output c_out
);

  wire and_1_out, and_2_out, and_3_out;

  and and_1 (and_1_out, a, b);
  and and_2 (and_2_out, b, c_in);
  and and_3 (and_3_out, a, c_in);
  or or_1 (c_out, and_1_out, and_2_out, and_3_out);
endmodule
